// Logisim project 4.circ as structural Verilog
module REG_Transmission (
);

  wire B_q, button_1_out;

  Button button_1 (.out(button_1_out));
  D_Flip_Flop A (.D(B_q), .clk(button_1_out));  // open: Q, Qn, preset, reset
  D_Flip_Flop B (.D(B_q), .clk(button_1_out), .Q(B_q));  // open: Qn, preset, reset

  // Notes on the sheet:
  //   A register: 1
  //   B register:1
  //   command: cp
endmodule

module REG_Transmission_fromA (
);

  wire A_q, button_1_out;

  Button button_1 (.out(button_1_out));
  D_Flip_Flop A (.D(A_q), .clk(button_1_out), .Q(A_q));  // open: Qn, preset, reset
  D_Flip_Flop B (.D(A_q), .clk(button_1_out));  // open: Q, Qn, preset, reset
endmodule

module REG_Switch (
);

  wire A_q, button_1_out, button_2_out, d_ff_2_q;

  Button button_1 (.out(button_1_out));
  D_Flip_Flop A (.D(A_q), .clk(button_1_out), .Q(A_q));  // open: Qn, preset, reset
  D_Flip_Flop B (.D(A_q), .clk(button_1_out));  // open: Q, Qn, preset, reset
  Button button_2 (.out(button_2_out));
  D_Flip_Flop d_ff_1 (.D(d_ff_2_q), .clk(button_2_out));  // open: Q, Qn, preset, reset
  D_Flip_Flop d_ff_2 (.D(d_ff_2_q), .clk(button_2_out), .Q(d_ff_2_q));  // open: Qn, preset, reset
endmodule
