// Logisim project class_report_bp21042.circ as structural Verilog
module sel2_1 (
  input  C1,
  input  C2,
  input  SEL,
  output Y
);

  wire and_1_out, and_2_out, not_1_out;

  not not_1 (not_1_out, SEL);
  and and_1 (and_1_out, C1, not_1_out);
  and and_2 (and_2_out, SEL, C2);
  or or_1 (Y, and_1_out, and_2_out);
endmodule

module sel4_1 (
  input  C1,
  input  C2,
  input  C3,
  input  C4,
  input  SEL1,
  input  SEL0,
  output Y
);

  wire and_1_out, and_2_out, and_3_out, and_4_out, not_1_out, not_2_out, not_3_out, not_4_out;

  not not_1 (not_1_out, SEL1);
  not not_2 (not_2_out, SEL0);
  not not_3 (not_3_out, SEL1);
  not not_4 (not_4_out, SEL0);
  and and_1 (and_1_out, C1, not_1_out, not_2_out);
  and and_2 (and_2_out, C2, not_3_out, SEL0);
  and and_3 (and_3_out, C3, SEL1, not_4_out);
  and and_4 (and_4_out, C4, SEL1, SEL0);
  or or_1 (Y, and_1_out, and_2_out, and_3_out, and_4_out);
endmodule

module ALU_1 (
  input  A,
  input  B,
  input  SEL2,
  input  SEL3,
  output out_5
);

  wire and_1_out, not_1_out, or_1_out, xor_1_out;

  and and_1 (and_1_out, A, B);
  or or_1 (or_1_out, A, B);
  xor xor_1 (xor_1_out, A, B);
  not not_1 (not_1_out, A);
  sel4_1 sel4_1_1 (.C1(and_1_out), .C2(or_1_out), .C3(xor_1_out), .C4(not_1_out), .SEL1(SEL2), .SEL0(SEL3), .Y(out_5));
endmodule

module HALF_ADDER (
  input  A,
  input  B,
  output sum,
  output carry
);

  xor xor_1 (sum, A, B);
  and and_1 (carry, A, B);
endmodule

module FULL_ADDER (
  input  A,
  input  B,
  input  ci,
  output sum,
  output cout
);

  wire and_1_out, and_2_out, xor_1_out;

  xor xor_1 (xor_1_out, A, B);
  xor xor_2 (sum, xor_1_out, ci);
  and and_1 (and_1_out, xor_1_out, ci);
  and and_2 (and_2_out, A, B);
  or or_1 (cout, and_1_out, and_2_out);
endmodule

module ADDER_4 (
  input  A3,
  input  A2,
  input  A1,
  input  A0,
  input  B3,
  input  B2,
  input  B1,
  input  B0,
  output Z3,
  output Z2,
  output Z1,
  output Z0,
  output overflow
);

  wire full_adder_1_cout, full_adder_2_cout, half_adder_1_carry;

  HALF_ADDER half_adder_1 (.A(A0), .B(B0), .sum(Z0), .carry(half_adder_1_carry));
  FULL_ADDER full_adder_1 (.A(A1), .B(B1), .ci(half_adder_1_carry), .sum(Z1), .cout(full_adder_1_cout));
  FULL_ADDER full_adder_2 (.A(A2), .B(B2), .ci(full_adder_1_cout), .sum(Z2), .cout(full_adder_2_cout));
  FULL_ADDER full_adder_3 (.A(A3), .B(B3), .ci(full_adder_2_cout), .sum(Z3), .cout(overflow));
endmodule

module COMPARATOR_2 (
  input  X1,
  input  X0,
  input  Y1,
  input  Y0,
  output C,
  output ZR
);

  wire and_1_out, and_2_out, and_3_out, and_4_out, and_5_out, and_6_out;

  and and_1 (and_1_out, X1, ~Y1);  // AND_Gate
  and and_2 (and_2_out, X0, ~Y0, ~Y1);  // AND_Gate
  and and_3 (and_3_out, X1, X0, ~Y0);  // AND_Gate
  and and_4 (and_4_out, Y1, ~X1);  // AND_Gate
  and and_5 (and_5_out, Y0, ~X1, ~X0);  // AND_Gate
  and and_6 (and_6_out, Y1, Y0, ~X0);  // AND_Gate
  or or_1 (C, and_1_out, and_2_out, and_3_out);
  or or_2 (ZR, and_4_out, and_5_out, and_6_out);
endmodule

module COMPARATOR_4 (
  input  X3,
  input  X2,
  input  X1,
  input  X0,
  input  Y3,
  input  Y2,
  input  Y1,
  input  Y0
);

  // COMPARATOR_2 comparator_2_1: pin names not known
endmodule

module ALU_4 (
  input  [3:0] A,
  input  [3:0] B,
  input  [2:0] OP,
  output Z3,
  output Z2,
  output Z1,
  output Z0
);

  wire adder_4_1_overflow, and_1_out, and_2_out, and_3_out, and_4_out, not_1_out, not_2_out, not_3_out,
       not_4_out, or_1_out, or_2_out, or_3_out, or_4_out, tAdderZ0, tAdderZ1, tAdderZ2, tAdderZ3, tLogicZ0,
       tLogicZ1, tLogicZ2, tLogicZ3, xor_1_out, xor_2_out, xor_3_out, xor_4_out;

  and and_1 (and_1_out, A[3], B[3]);
  or or_1 (or_1_out, A[3], B[3]);
  xor xor_1 (xor_1_out, A[3], B[3]);
  not not_1 (not_1_out, A[3]);
  and and_2 (and_2_out, A[2], B[2]);
  or or_2 (or_2_out, A[2], B[2]);
  xor xor_2 (xor_2_out, A[2], B[2]);
  not not_2 (not_2_out, A[2]);
  and and_3 (and_3_out, A[1], B[1]);
  or or_3 (or_3_out, A[1], B[1]);
  xor xor_3 (xor_3_out, A[1], B[1]);
  not not_3 (not_3_out, A[1]);
  and and_4 (and_4_out, A[0], B[0]);
  or or_4 (or_4_out, A[0], B[0]);
  xor xor_4 (xor_4_out, A[0], B[0]);
  not not_4 (not_4_out, A[0]);
  sel4_1 sel4_1_1 (
    .C1(and_1_out), .C2(or_1_out), .C3(xor_1_out), .C4(not_1_out), .SEL1(OP[1]), .SEL0(OP[0]), .Y(tLogicZ3));
  sel4_1 sel4_1_2 (
    .C1(and_2_out), .C2(or_2_out), .C3(xor_2_out), .C4(not_2_out), .SEL1(OP[1]), .SEL0(OP[0]), .Y(tLogicZ2));
  sel4_1 sel4_1_3 (
    .C1(and_3_out), .C2(or_3_out), .C3(xor_3_out), .C4(not_3_out), .SEL1(OP[1]), .SEL0(OP[0]), .Y(tLogicZ1));
  sel4_1 sel4_1_4 (
    .C1(and_4_out), .C2(or_4_out), .C3(xor_4_out), .C4(not_4_out), .SEL1(OP[1]), .SEL0(OP[0]), .Y(tLogicZ0));
  sel2_1 sel2_1_1 (.C1(tLogicZ3), .C2(tAdderZ3), .SEL(OP[2]), .Y(Z3));
  sel2_1 sel2_1_2 (.C1(tLogicZ2), .C2(tAdderZ2), .SEL(OP[2]), .Y(Z2));
  sel2_1 sel2_1_3 (.C1(tLogicZ1), .C2(tAdderZ1), .SEL(OP[2]), .Y(Z1));
  sel2_1 sel2_1_4 (.C1(tLogicZ0), .C2(tAdderZ0), .SEL(OP[2]), .Y(Z0));
  ADDER_4 adder_4_1 (
    .A3(A[3]), .A2(A[2]), .A1(A[1]), .A0(A[0]), .B3(B[3]), .B2(B[2]), .B1(B[1]), .B0(B[0]), .Z3(tAdderZ3),
    .Z2(tAdderZ2), .Z1(tAdderZ1), .Z0(tAdderZ0), .overflow(adder_4_1_overflow));
  // AND_Gate and_5 has open pins: in0=OP[2], in1=OP[1], in2=OP[0], in3=adder_4_1_overflow, out=open
  // AND_Gate and_6 has open pins: in0=OP[2], in1=OP[1], in2=OP[0], out=open

  // Other names for the same wires on the sheet: tA0 = A[0]; tA1 = A[1]; tA2 = A[2]; tA3 = A[3]; tB0 = B[0];
  //   tB1 = B[1]; tB2 = B[2]; tB3 = B[3]; top3 = OP[0]; top2 = OP[1]; top1 = OP[2]
endmodule

module reg_exp1 (
  input  Din,
  input  in_2,
  input  val,
  input  SEL2,
  input  SEL1,
  output out_6,
  output Dout
);

  wire button_1_out, button_2_out, button_3_out, button_4_out, button_5_out, button_6_out, CLOCK_out,
       d_ff_1_q, d_ff_2_q, d_ff_3_q, d_ff_4_q, not_1_out, not_2_out, not_3_out, RESET_out, sel2_1_1_y;

  Button CLOCK (.out(CLOCK_out));
  Button RESET (.out(RESET_out));
  not not_1 (not_1_out, d_ff_1_q);
  D_Flip_Flop d_ff_1 (.D(not_1_out), .clk(button_1_out), .Q(d_ff_1_q), .reset(button_2_out));  // open: Qn, preset
  Button button_1 (.out(button_1_out));
  Button button_2 (.out(button_2_out));
  D_Flip_Flop d_ff_2 (.D(Din), .clk(CLOCK_out), .Q(d_ff_2_q), .reset(RESET_out));  // open: Qn, preset
  LED led_1 (.in(d_ff_1_q));
  sel2_1 sel2_1_1 (.C1(Dout), .C2(val), .SEL(SEL2), .Y(sel2_1_1_y));
  LED led_2 (.in(d_ff_2_q));
  D_Flip_Flop d_ff_3 (.D(sel2_1_1_y), .clk(button_3_out), .Q(d_ff_3_q), .reset(button_4_out));  // open: Qn, preset
  Button button_3 (.out(button_3_out));
  Button button_4 (.out(button_4_out));
  D_Flip_Flop d_ff_4 (.D(out_6), .clk(button_5_out), .Q(d_ff_4_q), .reset(button_6_out));  // open: Qn, preset
  Button button_5 (.out(button_5_out));
  Button button_6 (.out(button_6_out));
  not not_2 (not_2_out, d_ff_3_q);
  not not_3 (not_3_out, d_ff_4_q);
  sel2_1 sel2_1_2 (.C1(d_ff_4_q), .C2(not_3_out), .SEL(in_2), .Y(out_6));
  sel2_1 sel2_1_3 (.C1(d_ff_3_q), .C2(not_2_out), .SEL(SEL1), .Y(Dout));
endmodule

module REG_Transmission (
);

  wire B_q, button_1_out;

  Button button_1 (.out(button_1_out));
  D_Flip_Flop A (.D(B_q), .clk(button_1_out));  // open: Q, Qn, preset, reset
  D_Flip_Flop B (.D(B_q), .clk(button_1_out), .Q(B_q));  // open: Qn, preset, reset
endmodule

module REG_Transmission_fromA (
);

  wire A_q, button_1_out;

  Button button_1 (.out(button_1_out));
  D_Flip_Flop A (.D(A_q), .clk(button_1_out), .Q(A_q));  // open: Qn, preset, reset
  D_Flip_Flop B (.D(A_q), .clk(button_1_out));  // open: Q, Qn, preset, reset
endmodule

module REG_Switch (
  input  RST,
  input  SEL1,
  input  SEL2,
  input  SEL3
);

  wire button_1_out, d_ff_1_q, d_ff_2_q, sel2_1_1_y, sel2_1_2_y, sel2_1_3_y;

  Button button_1 (.out(button_1_out));
  sel2_1 sel2_1_1 (.C1(d_ff_1_q), .C2(sel2_1_3_y), .SEL(SEL1), .Y(sel2_1_1_y));
  sel2_1 sel2_1_2 (.C1(d_ff_2_q), .C2(sel2_1_3_y), .SEL(SEL2), .Y(sel2_1_2_y));
  D_Flip_Flop d_ff_1 (.D(sel2_1_1_y), .clk(button_1_out), .Q(d_ff_1_q), .reset(RST));  // open: Qn, preset
  D_Flip_Flop d_ff_2 (.D(sel2_1_2_y), .clk(button_1_out), .Q(d_ff_2_q), .reset(RST));  // open: Qn, preset
  sel2_1 sel2_1_3 (.C1(d_ff_1_q), .C2(d_ff_2_q), .SEL(SEL3), .Y(sel2_1_3_y));

  // Other names for the same wires on the sheet: tRST = RST
endmodule

module REG_4 (
  input  SEL1,
  input  SEL2,
  input  SEL5_1,
  input  SEL5_2,
  input  SEL3,
  input  SEL4
);

  wire regA_q, regB_q, regC_q, regD_q, sel2_1_1_y, sel2_1_2_y, sel2_1_3_y, sel2_1_4_y, sel4_1_1_y, tCLK, tRST;

  Button button_1 (.out(tRST));
  Button button_2 (.out(tCLK));
  sel2_1 sel2_1_1 (.C1(regA_q), .C2(sel4_1_1_y), .SEL(SEL1), .Y(sel2_1_1_y));
  sel2_1 sel2_1_2 (.C1(regB_q), .C2(sel4_1_1_y), .SEL(SEL2), .Y(sel2_1_2_y));
  sel2_1 sel2_1_3 (.C1(regC_q), .C2(sel4_1_1_y), .SEL(SEL3), .Y(sel2_1_3_y));
  sel2_1 sel2_1_4 (.C1(regD_q), .C2(sel4_1_1_y), .SEL(SEL4), .Y(sel2_1_4_y));
  D_Flip_Flop regA (.D(sel2_1_1_y), .clk(tCLK), .Q(regA_q), .reset(tRST));  // open: Qn, preset
  D_Flip_Flop regB (.D(sel2_1_2_y), .clk(tCLK), .Q(regB_q), .reset(tRST));  // open: Qn, preset
  D_Flip_Flop regC (.D(sel2_1_3_y), .clk(tCLK), .Q(regC_q), .reset(tRST));  // open: Qn, preset
  D_Flip_Flop regD (.D(sel2_1_4_y), .clk(tCLK), .Q(regD_q), .reset(tRST));  // open: Qn, preset
  sel4_1 sel4_1_1 (.C1(regA_q), .C2(regB_q), .C3(regC_q), .C4(regD_q), .SEL1(SEL5_1), .SEL0(SEL5_2), .Y(sel4_1_1_y));
endmodule
